# Fritzing sketch SmartHome (saved by Fritzing 0.9.5d)
breadboards: 1

parts:
  WeMos_D1_Mini1 = WeMos D1 Mini
  KY-1 = Keyes Relay [package=THT]
  DHT11_1 = DHT11 module
  LED1 = LED - 3mm [color="Red (633nm)" package="3 mm [THT]"]
  R1 = Resistor [tolerance=±5% resistance=220 package="0805 [SMD]"]
  M1 = DC Motor
  S1 = Pushbutton [package="[SMD]"]
  S2 = Pushbutton [package="[SMD]"]
  R2 = Resistor [tolerance=±5% resistance=10k package="0805 [SMD]"]
  R3 = Resistor [tolerance=±5% resistance=10k package="0805 [SMD]"]

nets:
  5V: WeMos_D1_Mini1.5V, KY-1.signal, DHT11_1.VCC, S1.Pin_1, S1.Pin_2, S2.Pin_3, S2.Pin_4
  N1: WeMos_D1_Mini1.D1, KY-1.ground
  N2: WeMos_D1_Mini1.D2, DHT11_1.DATA
  N3: WeMos_D1_Mini1.D3, R1.Pin_0
  N4: WeMos_D1_Mini1.D4, S1.Pin_3, S1.Pin_4, R2.Pin_0
  N5: WeMos_D1_Mini1.D5, S2.Pin_1, S2.Pin_2, R3.Pin_0
  N6: WeMos_D1_Mini1.G, KY-1.power, DHT11_1.GND, LED1.cathode, R2.Pin_1, R3.Pin_1
  N7: KY-1.C, M1.pin_1
  N8: KY-1.NO, M1.pin_2
  N9: LED1.anode, R1.Pin_1

notes:
  Датчик температуры и влажности DHT11
  Микроконтроллер Wemos D1 mini
  Модуль реле
  Вентилятор
  Светодиод индикации низкой влажности
  Резистор на светодиод - 220 Ом
  Резисторы на кнопки - 10 кОм
  Кнопка фикс. темп.
  Кнопка фикс. влаж.

custom parts:
  Keyes Relay: The Keyes 5V relay module is suitable for SCM development, home appliance control. It uses a 5V~12V TIL control signal which can control DC / AC signal.
  DHT11 module: DHT11 black pcb module
